// Logisim project aiAlu.circ as structural Verilog: 6 circuits, main circuit and8bit
module and8bit (
  input  [7:0] in_1,
  input  [7:0] in_2,
  output [7:0] out_3
);

  assign out_3 = in_1 & in_2;  // AND_Gate and_1, 8 bits wide
endmodule

module or8bit (
  input  [7:0] in_1,
  input  [7:0] in_2,
  output [7:0] out_3
);

  assign out_3 = in_1 | in_2;  // OR_Gate or_1, 8 bits wide
endmodule

module not8bit (
  input  S2,
  input  S1,
  input  S0,
  input  D0,
  input  D1,
  input  D2,
  input  D3,
  input  D4,
  input  D5,
  input  D6,
  input  D7
);

  wire not_1_out, not_2_out, not_3_out;

  not not_1 (not_1_out, S2);
  not not_2 (not_2_out, S1);
  not not_3 (not_3_out, S0);
endmodule

module xor8bit (
  input  [7:0] in_1,
  input  [7:0] in_2,
  output [7:0] out_3
);

  wire [7:0] or_1_out;

  assign out_3 = ~or_1_out;  // NOT_Gate not_1, 8 bits wide
  assign or_1_out = in_1 | in_2;  // OR_Gate or_1, 8 bits wide
endmodule

module halfAdder (
  input  a,
  input  b,
  output S,
  output C
);

  and and_1 (C, a, b);
  xor xor_1 (S, a, b);
endmodule

module Full_Adder (
  input  C0,
  input  a,
  input  b,
  output S,
  output C1
);

  wire and_1_out, and_2_out, and_3_out, xor_1_out;

  xor xor_1 (xor_1_out, a, b);
  and and_1 (and_1_out, C0, a);
  and and_2 (and_2_out, a, b);
  and and_3 (and_3_out, C0, b);
  xor xor_2 (S, xor_1_out, C0);
  or or_1 (C1, and_1_out, and_2_out, and_3_out);
endmodule
